# Fritzing sketch Untitled Sketch (saved by Fritzing 0.9.2b)

parts:
  SparkFun_OpenScale1 = openScale_v04 [part_number=SEN-13261]
  Part1 = OpenLog

nets:
  GND: SparkFun_OpenScale1.GND, Part1.GND
  N1: SparkFun_OpenScale1.TXD, Part1.RXI
  5V: SparkFun_OpenScale1.5V, Part1.VCC

notes:
  Load Cell

custom parts:
  openScale_v04: OpenScale is an open source hardware load cell reader and calibration device. It has the ability to read multiple types of load cells and offers a simple to use serial menu to configure calibration value, sample rate, time stamp, and units of precision.
